// Logisim project Logic_CKT.circ as structural Verilog: 1 circuit, main circuit main
module main (
  input  L1,
  input  L0,
  input  C0,
  input  R0,
  input  R1,
  output ML0,
  output ML1,
  output MR0,
  output MR1
);

  wire and_1_out, and_2_out, and_3_out, and_4_out, and_5_out, and_6_out, and_7_out, and_8_out, and_9_out,
       and_10_out, and_11_out, and_12_out, and_13_out, and_14_out, not_1_out, not_2_out, not_3_out,
       not_4_out, or_1_out, or_2_out;

  not not_1 (not_1_out, L1);
  not not_2 (not_2_out, L0);
  not not_3 (not_3_out, C0);
  not not_4 (not_4_out, R1);
  and and_1 (and_1_out, not_1_out, not_2_out);
  and and_2 (and_2_out, L1, L0);
  and and_3 (and_3_out, L0, not_4_out);
  and and_4 (and_4_out, L1, L0);
  and and_5 (and_5_out, R0, R1);
  and and_6 (and_6_out, and_1_out, R0);
  and and_7 (and_7_out, L1, not_3_out);
  and and_8 (and_8_out, and_2_out, C0);
  and and_9 (and_9_out, R0, R1);
  or or_1 (or_1_out, C0, and_3_out);
  and and_10 (and_10_out, L1, not_4_out);
  and and_11 (and_11_out, not_3_out, R1);
  and and_12 (and_12_out, and_4_out, and_5_out);
  or or_2 (or_2_out, R1, and_6_out);
  and and_13 (and_13_out, and_7_out, not_4_out);
  and and_14 (and_14_out, and_8_out, and_9_out);
  or or_3 (MR0, or_1_out, and_10_out);
  or or_4 (MR1, and_11_out, and_12_out);
  or or_5 (ML0, or_2_out, C0);
  or or_6 (ML1, and_13_out, and_14_out);
endmodule
